# Fritzing sketch mashControlMotor (saved by Fritzing 0.9.3b)
circuit board: 2.41629cm x 3.16477cm
breadboards: 1

parts:
  part = L293D [package=THT]
  RPi = male pin header, 6 pins [form="♂ (male)"]
  Motor = male pin header, 4 pins [form="♂ (male)"]
  C1 = Electrolytic Capacitor [capacitance=10µF package="100 mil [THT, electrolytic]"]
  C3 = Electrolytic Capacitor [capacitance=100nF package="100 mil [THT, electrolytic]"]

nets:
  N1: part.Enable_1, part.Enable_2
  N2: part.In_1, RPi.pin2
  N3: part.0V, RPi.pin5, Motor.pin4, C1.-, C3.-
  N4: part.Out_2_(_Controlled_by_Enable_1_), Motor.pin3
  N5: part.In_2, RPi.pin1
  N6: part.+Vmotor, part.+V, RPi.pin6, C1.+, C3.+
  N7: part.In_3, RPi.pin3
  N8: part.Out_3_(_Controlled_by_Enable_2_), Motor.pin1
  N9: part.Out_4_(_Controlled_by_Enable_2_), Motor.pin2
  N10: part.In_4, RPi.pin4

notes:
  V G 4 3 1 2
  G 2 4 3
  P O B Y
  RPi
  L293D
