# Fritzing sketch mashControlds18b20 (saved by Fritzing 0.9.3b)
circuit board: 3.5cm x 1.7cm
breadboards: 1

parts:
  part = Resistor [tolerance=±5% resistance=4.7k package=THT]
  2 = male pin header, 3 pins [form="♂ (male)"]
  5 = male pin header, 3 pins [form="♂ (male)"]
  1 = male pin header, 3 pins [form="♂ (male)"]
  4 = male pin header, 3 pins [form="♂ (male)"]
  3 = male pin header, 3 pins [form="♂ (male)"]
  part_2 = male pin header, 3 pins [form="♂ (male)"]

nets (from the schematic view):
  N1: part.Pin_0, 2.pin2, 5.pin2, 1.pin2, 4.pin2, 3.pin2, part_2.pin2
  N2: part.Pin_1, 2.pin3, 5.pin3, 1.pin3, 4.pin3, 3.pin3, part_2.pin3
  N3: 5.pin1, 1.pin1, part_2.pin1

notes:
  RPi V D G
  V D G
  ds18b20
  Mash Control, DS18B20 Series, 1
