# Fritzing sketch mashControl (saved by Fritzing 0.9.3b)
circuit board: 3.77609cm x 4.25833cm
breadboards: 1

parts:
  R1 = Resistor [tolerance=±5% resistance=4.7k package=THT]
  Thermometer = Molex Picoblade Series Header [part_number=0533980371 package=Picoblade-53398-0371]
  IC1 = L293D [package=THT]
  Motor = Molex Picoblade Series Header [part_number=0533980471 package=Picoblade-53398-0471]
  RPi_Thermometer = male pin header, 4 pins [form="♂ (male)"]
  RPi_Motor = male pin header, 6 pins [form="♂ (male)"]

nets (from the breadboard view):
  N1: R1.Pin_0, Thermometer.2, RPi_Thermometer.pin3
  N2: R1.Pin_1, Thermometer.1, RPi_Thermometer.pin4
  N3: Thermometer.3, RPi_Thermometer.pin2
  N4: IC1.Enable_1, IC1.Enable_2
  N5: IC1.In_1, RPi_Motor.pin3
  N6: IC1.Out_1_(_Controlled_by_Enable_1_), Motor.1
  N7: IC1.0V, RPi_Motor.pin2
  N8: IC1.Out_2_(_Controlled_by_Enable_1_), Motor.2
  N9: IC1.In_2, RPi_Motor.pin1
  N10: IC1.+Vmotor, IC1.+V, RPi_Motor.pin4
  N11: IC1.In_3, RPi_Motor.pin6
  N12: IC1.Out_3_(_Controlled_by_Enable_2_), Motor.3
  N13: IC1.Out_4_(_Controlled_by_Enable_2_), Motor.4
  N14: IC1.In_4, RPi_Motor.pin5

notes:
  ds18b connection
  Motor connection
