# Fritzing sketch mashControlBreadboard (saved by Fritzing 0.9.3b)
breadboards: 1

parts:
  Raspberry_Pi_1 = Raspberry Pi 3 [part_number=RPI-3-V1.2]
  R1 = Resistor [tolerance=±5% resistance=4.7k package=THT]
  U1 = Molex Picoblade Series Header [part_number=0533980371 package=Picoblade-53398-0371]
  IC1 = L293D [package=THT]
  U2 = Molex Picoblade Series Header [part_number=0533980471 package=Picoblade-53398-0471]
  Part2 = Adafruit T-Cobbler Plus [part_number="Adafruit #1989 and #2028"]
  MOTOR1 = Adafruit Gear-Reduced Stepper Motor (small)
  DS1 = DS18B20 1-Wire Temperature Sensor [part_number=DS18B20]
  U3 = Molex Picoblade Series Header [part_number=0533980371 package=Picoblade-53398-0371]
  U4 = Molex Picoblade Series Header [part_number=0533980471 package=Picoblade-53398-0471]
  U5 = 4-Channel 5v Relay Shield [package=relay-4ch5v10a]
  VALVE1 = Plastic Solenoid Valve

nets:
  3V3: Raspberry_Pi_1.3v3, Raspberry_Pi_1.3V3, R1.Pin_1, U1.1, Part2.+3.3V, Part2.+3.3V_2, U5.K2-Off, U5.K3-Off
  N1: Raspberry_Pi_1.GPIO2, Part2.SDA
  N2: Raspberry_Pi_1.GPIO3, Part2.SCL
  N3: Raspberry_Pi_1.GPIO4, IC1.In_1, Part2.GPIO4
  GND: Raspberry_Pi_1.GND, U1.3, IC1.0V, Part2.GND, U5.GND
  N4: Raspberry_Pi_1.GPIO17, IC1.In_2, Part2.GPIO17
  N5: Raspberry_Pi_1.GPIO27, Part2.GPIO27, U5.IN1
  N6: Raspberry_Pi_1.GPIO22, Part2.GPIO22
  N7: Raspberry_Pi_1.GPIO10, Part2.MOSI
  N8: Raspberry_Pi_1.GPIO9, Part2.MISO
  N9: Raspberry_Pi_1.GPIO11, Part2.SCLK
  N10: Raspberry_Pi_1.ID_SD, Part2.EEDAT
  N11: Raspberry_Pi_1.GPIO5, R1.Pin_0, U1.2, Part2.GPIO5
  N12: Raspberry_Pi_1.GPIO6, Part2.GPIO6, U5.IN4
  N13: Raspberry_Pi_1.GPIO13, Part2.GPIO13, U5.IN3
  N14: Raspberry_Pi_1.GPIO19, Part2.GPIO19, U5.IN2
  N15: Raspberry_Pi_1.GPIO26, Part2.GPIO26
  N16: Raspberry_Pi_1.GPIO21, Part2.GPIO21
  N17: Raspberry_Pi_1.GPIO20, Part2.GPIO20
  N18: Raspberry_Pi_1.GPIO16, Part2.GPIO16
  N19: Raspberry_Pi_1.GPIO12, Part2.GPIO12
  N20: Raspberry_Pi_1.ID_SC, Part2.EECLK
  N21: Raspberry_Pi_1.GPIO7, Part2.CE1
  N22: Raspberry_Pi_1.GPIO8, Part2.CE0
  N23: Raspberry_Pi_1.GPIO25, Part2.GPIO25
  N24: Raspberry_Pi_1.GPIO24, IC1.In_3, Part2.GPIO24
  N25: Raspberry_Pi_1.GPIO23, IC1.In_4, Part2.GPIO23
  N26: Raspberry_Pi_1.GPIO18, Part2.GPIO18
  N27: Raspberry_Pi_1.GPIO15, Part2.RXD
  N28: Raspberry_Pi_1.GPIO14, Part2.TXD
  5V: Raspberry_Pi_1.5V, IC1.+Vmotor, IC1.+V, Part2.+5V, U5.VCC
  N29: IC1.Enable_1, IC1.Enable_2
  N30: IC1.Out_1_(_Controlled_by_Enable_1_), U2.2
  N31: IC1.Out_2_(_Controlled_by_Enable_1_), U2.1
  N32: IC1.Out_3_(_Controlled_by_Enable_2_), U2.4
  N33: IC1.Out_4_(_Controlled_by_Enable_2_), U2.3
  N34: MOTOR1.ORANGE, U4.4
  N35: MOTOR1.YELLOW, U4.1
  N36: MOTOR1.PINK, U4.3
  N37: MOTOR1.BLUE, U4.2
  N38: DS1.VDD, U3.3
  N39: DS1.DQ, U3.2
  N40: DS1.GND, U3.1
  N41: U5.K4-On, VALVE1.no_name_yet#2

notes:
  ds18b connection
  Motor connection
  Any number of ds18b can be added
  12VDC, 2A Power Supply
  Induction Cooker
  Pump

custom parts:
  Adafruit T-Cobbler Plus: The Raspberry Pi has landed on the Maker World like a 40-GPIO pinned, quad-USB ported, credit card sized bomb of DIY joy. And while you can use most of our great Model B accessories by hooking up our downgrade cable, its probably a good time to upgrade your set up and accessorize using all of the 40 pins. That's why we now carry the Assembled Adafruit Pi T-Cobbler Plus - Breakout + Cable for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
  Adafruit Gear-Reduced Stepper Motor (small): Adafruit gear-reduction stepper motor (small)
  4-Channel 5v Relay Shield: 4 Channel 5v Relay Shield w. 2x SPD-06VDC-SD-C
