# Fritzing sketch mashControlBreadboard2 (saved by Fritzing 0.9.3b)
circuit board: 5.42489cm x 3.15262cm
breadboards: 1

parts:
  Raspberry_Pi_1 = Raspberry Pi 3 [part_number=RPI-3-V1.2]
  R1 = Resistor [tolerance=±5% resistance=4.7k package=THT]
  Motor_Ctrl = L293D [package=THT]
  DS1 = DS18B20 1-Wire Temperature Sensor [part_number=DS18B20]  # not connected
  U5 = 4-Channel 5v Relay Shield [package=relay-4ch5v10a]  # not connected
  3_3V = female pin header, 4 pins [form="♀ (female)"]
  Relay = female pin header, 6 pins [form="♀ (female)"]
  J2 = female pin header, 3 pins [form="♀ (female)"]
  J6 = female pin header, 3 pins [form="♀ (female)"]
  Motor = female pin header, 4 pins [form="♀ (female)"]
  DS18B20 = female pin header, 3 pins [form="♀ (female)"]
  C1 = Electrolytic Capacitor [capacitance=1µF package="100 mil [THT, electrolytic]"]
  C2 = Electrolytic Capacitor [capacitance=1µF package="100 mil [THT, electrolytic]"]

nets (from the pcb view):
  3V3: Raspberry_Pi_1.3v3, Raspberry_Pi_1.3V3, R1.Pin_1, 3_3V.pin1, 3_3V.pin2, 3_3V.pin3, 3_3V.pin4, J2.pin3, J6.pin3, DS18B20.pin3, C1.+
  N1: Raspberry_Pi_1.GPIO17, Motor_Ctrl.In_4
  N2: Raspberry_Pi_1.GPIO27, Motor_Ctrl.In_3
  N3: Raspberry_Pi_1.GPIO22, Motor_Ctrl.Enable_1, Motor_Ctrl.Enable_2
  N4: Raspberry_Pi_1.GPIO10, Motor_Ctrl.In_2
  N5: Raspberry_Pi_1.GPIO11, Motor_Ctrl.In_1
  N6: Raspberry_Pi_1.GND, Motor_Ctrl.0V, Relay.pin1, J2.pin1, J6.pin1, DS18B20.pin1, C1.-, C2.-
  N7: Raspberry_Pi_1.GPIO5, R1.Pin_0, J2.pin2, J6.pin2, DS18B20.pin2
  N8: Raspberry_Pi_1.GPIO6, Relay.pin5
  N9: Raspberry_Pi_1.GPIO13, Relay.pin4
  N10: Raspberry_Pi_1.GPIO19, Relay.pin3
  N11: Raspberry_Pi_1.GPIO26, Relay.pin2
  N12: Raspberry_Pi_1.5V, Motor_Ctrl.+Vmotor, Motor_Ctrl.+V, Relay.pin6, C2.+
  N13: Motor_Ctrl.Out_1_(_Controlled_by_Enable_1_), Motor.pin2
  N14: Motor_Ctrl.Out_2_(_Controlled_by_Enable_1_), Motor.pin1
  N15: Motor_Ctrl.Out_3_(_Controlled_by_Enable_2_), Motor.pin4
  N16: Motor_Ctrl.Out_4_(_Controlled_by_Enable_2_), Motor.pin3

notes:
  ds18b connection
  Motor connection
  Any number of ds18b can be added
  V D G
  23
  4
  17
  Mash Control v1
  Pump
  Mode
  Heater
  Chiller
  5V
  Gnd

custom parts:
  4-Channel 5v Relay Shield: 4 Channel 5v Relay Shield w. 2x SPD-06VDC-SD-C
