# Fritzing sketch mashControlds18b20 (saved by Fritzing 0.9.3b)
circuit board: 3.74899cm x 1.71806cm
breadboards: 1

parts:
  R1 = Resistor [tolerance=±5% resistance=4.7k package=THT]
  2 = male pin header, 3 pins [form="♂ (male)"]
  5 = male pin header, 3 pins [form="♂ (male)"]
  1 = male pin header, 3 pins [form="♂ (male)"]
  4 = male pin header, 3 pins [form="♂ (male)"]
  3 = male pin header, 3 pins [form="♂ (male)"]
  J1 = male pin header, 3 pins [form="♂ (male)"]
  C1 = Electrolytic Capacitor [capacitance=1µF package="100 mil [THT, electrolytic]"]

nets:
  N1: R1.Pin_0, 2.pin1, 5.pin1, 1.pin1, 4.pin1, 3.pin1, J1.pin1
  N2: R1.Pin_1, 2.pin3, 5.pin3, 1.pin3, 4.pin3, 3.pin3, J1.pin3, C1.+
  N3: 2.pin2, 5.pin2, 1.pin2, 4.pin2, 3.pin2, J1.pin2, C1.-

notes:
  V G D
  ds18b20
  Mash Control, DS18B20 Series, 2
  RPi
